# Fritzing sketch server (saved by Fritzing 0.9.2b)
breadboards: 2

parts:
  Raspberry_Pi1 = Raspberry Pi 2
  TX433 = TSOP312.., 314.. [package=THT]
  Power_LED = smd LED [color="Red (633nm)" package="1206 [SMD]"]
  R1 = Resistor [tolerance=±5% resistance=220 package="2512 [SMD]"]
  SELECT = Pushbutton [package="[SMD]"]
  7SEG2 = 7-Segment LED I2C Backpack (red)
  RX433 = TSOP312.., 314.. [package=THT]
  MODE = Pushbutton [package="[SMD]"]

nets:
  3V3: Raspberry_Pi1.3v3, Raspberry_Pi1.3V3, SELECT.Pin_1, SELECT.Pin_2, RX433.Vs, MODE.Pin_1, MODE.Pin_2
  N1: Raspberry_Pi1.GPIO2, 7SEG2.SDA
  N2: Raspberry_Pi1.GPIO3, 7SEG2.SCL
  N3: Raspberry_Pi1.GPIO19, SELECT.Pin_3, SELECT.Pin_4
  N4: Raspberry_Pi1.GPIO26, MODE.Pin_3, MODE.Pin_4
  GND: Raspberry_Pi1.GND, TX433.GND, R1.Pin_0, 7SEG2.GND, RX433.GND
  N5: Raspberry_Pi1.GPIO21, TX433.Data
  N6: Raspberry_Pi1.GPIO20, Power_LED.anode
  N7: Raspberry_Pi1.GPIO12, RX433.Data
  N8: Raspberry_Pi1.5V, TX433.Vs, 7SEG2.V+
  N9: Power_LED.cathode, R1.Pin_1

custom parts:
  7-Segment LED I2C Backpack (red): 4-digit, 7-segment LED Display with I2C Control
